# Fritzing sketch ultrasonidos_RGB (saved by Fritzing 0.8.5b)
breadboards: 1

parts:
  Parte1 = Arduino Uno (Rev3)
  부품3 = HC-SR 04
  LED2 = RGB LED (com. cathode, rgb) [package="5 mm [THT]"]

nets:
  N1: Parte1.D9_PWM, LED2.red_anode
  N2: Parte1.D10_PWM/SS, LED2.common_cathode
  N3: Parte1.D11_PWM/MOSI, LED2.blue_anode
  N4: Parte1.D12/MISO, 부품3.Trig
  5V: Parte1.5V, 부품3.VCC
  GND: Parte1.GND, 부품3.GND, LED2.green_anode
